// Logisim project bcd - Copy.circ as structural Verilog: 8 circuits, main circuit implementation
module implementation (
  input  w3,
  input  w2,
  input  w1,
  input  w0,
  output a,
  output b,
  output c,
  output d,
  output e,
  output f,
  output g
);

  at_circuit at_circuit_1 (.w2_in(w2), .w0_in(w0), .w1_in(w1), .w3_in(w3), .at_out(a));
  bt_circuit bt_circuit_1 (.w2_in(w2), .w0_in(w0), .w1_in(w1), .bt_out(b));
  ct_circuit ct_circuit_1 (.w2_in(w2), .w1_in(w1), .w0_in(w0), .ct_out(c));
  dt_circuit dt_circuit_1 (.w0_in(w0), .w1_in(w1), .w2_in(w2), .w3_in(w3), .dt_output(d));
  et_circuit et_circuit_1 (.w2_in(w2), .w1_in(w1), .w0_in(w0), .et_output(e));
  ft_circuit ft_circuit_1 (.w0_in(w0), .w1_in(w1), .w2_in(w2), .w3_in(w3), .ft_output(f));
  gt_circuit gt_circuit_1 (.w0_in(w0), .w1_in(w1), .w2_in(w2), .w3_in(w3), .gt_output(g));

  // Other names for the same wires on the sheet: at = a; bt = b; ct = c; dt = d; et = e; ft = f; gt = g; w0t = w0;
  //   w1t = w1; w2t = w2; w3t = w3
endmodule

module at_circuit (
  input  w2_in,
  input  w0_in,
  input  w1_in,
  input  w3_in,
  output at_out
);

  wire and_1_out, and_2_out, not_1_out, not_2_out;

  not not_1 (not_1_out, w2_in);
  not not_2 (not_2_out, w0_in);
  and and_1 (and_1_out, not_1_out, not_2_out);
  and and_2 (and_2_out, w2_in, w0_in);
  or or_1 (at_out, and_1_out, and_2_out, w1_in, w3_in);
endmodule

module bt_circuit (
  input  w2_in,
  input  w0_in,
  input  w1_in,
  output bt_out
);

  wire and_1_out, and_2_out, not_1_out, not_2_out, not_3_out;

  not not_1 (not_1_out, w2_in);
  not not_2 (not_2_out, w0_in);
  not not_3 (not_3_out, w1_in);
  and and_1 (and_1_out, not_2_out, not_3_out);
  and and_2 (and_2_out, w1_in, w0_in);
  or or_1 (bt_out, not_1_out, and_1_out, and_2_out);
endmodule

module ct_circuit (
  input  w2_in,
  input  w1_in,
  input  w0_in,
  output ct_out
);

  wire not_1_out;

  not not_1 (not_1_out, w1_in);
  or or_1 (ct_out, w2_in, not_1_out, w0_in);
endmodule

module dt_circuit (
  input  w0_in,
  input  w1_in,
  input  w2_in,
  input  w3_in,
  output dt_output
);

  wire and_1_out, and_2_out, and_3_out, and_4_out, not_1_out, not_2_out, not_3_out, not_4_out, not_5_out;

  not not_1 (not_1_out, w2_in);
  not not_2 (not_2_out, w0_in);
  not not_3 (not_3_out, w0_in);
  not not_4 (not_4_out, w2_in);
  not not_5 (not_5_out, w1_in);
  and and_1 (and_1_out, not_1_out, w1_in);
  and and_2 (and_2_out, not_2_out, w1_in);
  and and_3 (and_3_out, not_3_out, not_4_out);
  and and_4 (and_4_out, not_5_out, w0_in, w2_in);
  or or_1 (dt_output, and_1_out, and_2_out, w3_in, and_3_out, and_4_out);

  // Other names for the same wires on the sheet: w0 = w0_in; w1 = w1_in; w2 = w2_in; w3 = w3_in
endmodule

module et_circuit (
  input  w2_in,
  input  w1_in,
  input  w0_in,
  output et_output
);

  wire and_1_out, and_2_out, not_1_out, not_2_out, not_3_out;

  not not_1 (not_1_out, w0_in);
  and and_1 (and_1_out, not_1_out, w1_in);
  not not_2 (not_2_out, w2_in);
  and and_2 (and_2_out, not_2_out, not_3_out);
  not not_3 (not_3_out, w0_in);
  or or_1 (et_output, and_1_out, and_2_out);

  // Other names for the same wires on the sheet: w0 = w0_in; w1 = w1_in; w2 = w2_in
endmodule

module ft_circuit (
  input  w0_in,
  input  w1_in,
  input  w2_in,
  input  w3_in,
  output ft_output
);

  wire and_1_out, and_2_out, and_3_out, not_1_out, not_2_out, not_3_out, not_4_out;

  not not_1 (not_1_out, w0_in);
  not not_2 (not_2_out, w1_in);
  not not_3 (not_3_out, w1_in);
  not not_4 (not_4_out, w0_in);
  and and_1 (and_1_out, not_1_out, not_2_out);
  and and_2 (and_2_out, not_3_out, w2_in);
  and and_3 (and_3_out, not_4_out, w2_in);
  or or_1 (ft_output, w3_in, and_1_out, and_2_out, and_3_out);

  // Other names for the same wires on the sheet: w0 = w0_in; w1 = w1_in; w2 = w2_in; w3 = w3_in
endmodule

module gt_circuit (
  input  w0_in,
  input  w1_in,
  input  w2_in,
  input  w3_in,
  output gt_output
);

  wire and_1_out, and_2_out, and_3_out, not_1_out, not_2_out, not_3_out;

  not not_1 (not_1_out, w0_in);
  not not_2 (not_2_out, w1_in);
  not not_3 (not_3_out, w2_in);
  and and_1 (and_1_out, not_1_out, w1_in);
  and and_2 (and_2_out, not_2_out, w2_in);
  and and_3 (and_3_out, not_3_out, w1_in);
  or or_1 (gt_output, w3_in, and_1_out, and_2_out, and_3_out);

  // Other names for the same wires on the sheet: w0 = w0_in; w1 = w1_in; w2 = w2_in; w3 = w3_in
endmodule
