// Logisim project adder4.circ as structural Verilog: 2 circuits, main circuit implementation
module implementation (
  input  [3:0] Ain,
  input  [3:0] Bin,
  input  Cinin,
  output [3:0] Sum_Out,
  output Carry_Out
);

  wire and_1_out, and_2_out, and_3_out, and_4_out, pg_1_g, pg_1_p, pg_2_g, pg_2_p, pg_3_g, pg_3_p, pg_4_g,
       pg_4_p, xor_2_out, xor_4_out, xor_6_out;

  xor xor_1 (Sum_Out[0], Bin[0], Ain[0], Cinin);
  PG pg_1 (.in_1({Bin[0], Ain[0]}), .G(pg_1_g), .P(pg_1_p));
  and and_1 (and_1_out, Cinin, pg_1_p);
  xor xor_2 (xor_2_out, and_1_out, pg_1_g);
  xor xor_3 (Sum_Out[1], Bin[1], Ain[1], xor_2_out);
  and and_2 (and_2_out, xor_2_out, pg_2_p);
  xor xor_4 (xor_4_out, and_2_out, pg_2_g);
  PG pg_2 (.in_1({Bin[1], Ain[1]}), .G(pg_2_g), .P(pg_2_p));
  xor xor_5 (Sum_Out[2], Bin[2], Ain[2], xor_4_out);
  PG pg_3 (.in_1({Bin[2], Ain[2]}), .G(pg_3_g), .P(pg_3_p));
  and and_3 (and_3_out, xor_4_out, pg_3_p);
  xor xor_6 (xor_6_out, and_3_out, pg_3_g);
  xor xor_7 (Sum_Out[3], Bin[3], Ain[3], xor_6_out);
  PG pg_4 (.in_1({Bin[3], Ain[3]}), .G(pg_4_g), .P(pg_4_p));
  and and_4 (and_4_out, xor_6_out, pg_4_p);
  or or_1 (Carry_Out, and_4_out, pg_4_g);

  // Other names for the same wires on the sheet: A[3:0] = Ain; AB0[1:0] = {Bin[0], Ain[0]};
  //   AB1[1:0] = {Bin[1], Ain[1]}; AB2[1:0] = {Bin[2], Ain[2]}; AB3[1:0] = {Bin[3], Ain[3]}; B[3:0] = Bin;
  //   C3 = Carry_Out; Cin = Cinin; Sum[3:0] = Sum_Out

  // Notes on the sheet:
  //   Carter Cooper
endmodule

module PG (
  input  [1:0] in_1,
  output G,
  output P
);

  and and_1 (G, in_1[0], in_1[1]);
  xor xor_1 (P, in_1[0], in_1[1]);
endmodule
