// Logisim project bitcounter.circ as structural Verilog: 1 circuit, main circuit implementation
module implementation (
  input  [7:0] BitsIn,
  input  CountZerosIn,
  output [3:0] BitCountOut
);

  wire [1:0] adder_1_out, adder_2_out, adder_3_out, adder_4_out, adder_5_out, adder_6_out;
  wire [2:2] adder_5_cout, adder_6_cout;
  wire [7:0] multiplexer_1_out, not_1_out;

  assign not_1_out = ~BitsIn;  // NOT_Gate not_1, 8 bits wide
  Multiplexer #(.enable("false"), .width(8)) multiplexer_1 (
    .in0(BitsIn), .in1(not_1_out), .out(multiplexer_1_out), .sel(CountZerosIn));
  Adder #(.width(1)) adder_1 (
    .a(multiplexer_1_out[0]), .b(multiplexer_1_out[1]), .out(adder_1_out[0]), .cout(adder_1_out[1]));  // open: cin
  Adder #(.width(1)) adder_2 (
    .a(multiplexer_1_out[2]), .b(multiplexer_1_out[3]), .out(adder_2_out[0]), .cout(adder_2_out[1]));  // open: cin
  Adder #(.width(1)) adder_3 (
    .a(multiplexer_1_out[4]), .b(multiplexer_1_out[5]), .out(adder_3_out[0]), .cout(adder_3_out[1]));  // open: cin
  Adder #(.width(1)) adder_4 (
    .a(multiplexer_1_out[6]), .b(multiplexer_1_out[7]), .out(adder_4_out[0]), .cout(adder_4_out[1]));  // open: cin
  Adder #(.width(2)) adder_5 (
    .a(adder_1_out), .b(adder_2_out), .out(adder_5_out), .cout(adder_5_cout[2]));  // open: cin
  Adder #(.width(2)) adder_6 (
    .a(adder_3_out), .b(adder_4_out), .out(adder_6_out), .cout(adder_6_cout[2]));  // open: cin
  Adder #(.width(3)) adder_7 (
    .a({adder_5_cout[2], adder_5_out}), .b({adder_6_cout[2], adder_6_out}), .out(BitCountOut[2:0]),
    .cout(BitCountOut[3]));  // open: cin

  // Other names for the same wires on the sheet: BitCount[3:0] = BitCountOut; Bits[7:0] = BitsIn;
  //   CountZeros = CountZerosIn

  // Notes on the sheet:
  //   Carter Cooper
endmodule
