// Logisim project shifter.circ as structural Verilog: 1 circuit, main circuit implementation
module implementation (
  input  IsRightShiftIn,
  input  IsArithmeticIn,
  input  [1:0] ShiftAmountIn,
  input  [2:0] NumberIn,
  output [2:0] ShiftedNumberOut
);

  wire multiplexer_2_out, multiplexer_3_out, multiplexer_4_out, multiplexer_5_out, multiplexer_7_out,
       multiplexer_8_out, multiplexer_9_out, multiplexer_11_out, multiplexer_12_out;

  Multiplexer #(.enable("false"), .select(2)) multiplexer_1 (
    .in0(NumberIn[2]), .in1(multiplexer_2_out), .in2(multiplexer_3_out), .in3(multiplexer_4_out),
    .out(ShiftedNumberOut[2]), .sel(ShiftAmountIn));
  Multiplexer #(.enable("false"), .select(2)) multiplexer_2 (
    .in0(NumberIn[1]), .in1(NumberIn[1]), .in2(1'b0), .in3(NumberIn[2]), .out(multiplexer_2_out),
    .sel({IsRightShiftIn, IsArithmeticIn}));
  Multiplexer #(.enable("false"), .select(2)) multiplexer_3 (
    .in0(NumberIn[0]), .in1(NumberIn[0]), .in2(1'b0), .in3(NumberIn[2]), .out(multiplexer_3_out),
    .sel({IsRightShiftIn, IsArithmeticIn}));
  Multiplexer #(.enable("false"), .select(2)) multiplexer_4 (
    .in0(1'b0), .in1(1'b0), .in2(1'b0), .in3(NumberIn[2]), .out(multiplexer_4_out),
    .sel({IsRightShiftIn, IsArithmeticIn}));
  Multiplexer #(.enable("false"), .select(2)) multiplexer_5 (
    .in0(NumberIn[0]), .in1(NumberIn[0]), .in2(NumberIn[2]), .in3(NumberIn[2]), .out(multiplexer_5_out),
    .sel({IsRightShiftIn, IsArithmeticIn}));
  Multiplexer #(.enable("false"), .select(2)) multiplexer_6 (
    .in0(NumberIn[1]), .in1(multiplexer_5_out), .in2(multiplexer_7_out), .in3(multiplexer_8_out),
    .out(ShiftedNumberOut[1]), .sel(ShiftAmountIn));
  Multiplexer #(.enable("false"), .select(2)) multiplexer_7 (
    .in0(1'b0), .in1(1'b0), .in2(1'b0), .in3(NumberIn[2]), .out(multiplexer_7_out),
    .sel({IsRightShiftIn, IsArithmeticIn}));
  Multiplexer #(.enable("false"), .select(2)) multiplexer_8 (
    .in0(1'b0), .in1(1'b0), .in2(1'b0), .in3(NumberIn[2]), .out(multiplexer_8_out),
    .sel({IsRightShiftIn, IsArithmeticIn}));
  Multiplexer #(.enable("false"), .select(2)) multiplexer_9 (
    .in0(1'b0), .in1(1'b0), .in2(NumberIn[1]), .in3(NumberIn[1]), .out(multiplexer_9_out),
    .sel({IsRightShiftIn, IsArithmeticIn}));
  Multiplexer #(.enable("false"), .select(2)) multiplexer_10 (
    .in0(NumberIn[0]), .in1(multiplexer_9_out), .in2(multiplexer_11_out), .in3(multiplexer_12_out),
    .out(ShiftedNumberOut[0]), .sel(ShiftAmountIn));
  Multiplexer #(.enable("false"), .select(2)) multiplexer_11 (
    .in0(1'b0), .in1(1'b0), .in2(NumberIn[2]), .in3(NumberIn[2]), .out(multiplexer_11_out),
    .sel({IsRightShiftIn, IsArithmeticIn}));
  Multiplexer #(.enable("false"), .select(2)) multiplexer_12 (
    .in0(1'b0), .in1(1'b0), .in2(1'b0), .in3(NumberIn[2]), .out(multiplexer_12_out),
    .sel({IsRightShiftIn, IsArithmeticIn}));

  // Other names for the same wires on the sheet: IsArithmetic = IsArithmeticIn; IsRightShift = IsRightShiftIn;
  //   Number[2:0] = NumberIn; ShiftAmount[1:0] = ShiftAmountIn; ShiftedNumber[2:0] = ShiftedNumberOut

  // Notes on the sheet:
  //   Carter Cooper
endmodule
