// Logisim project FourBitParity.circ as structural Verilog: 1 circuit, main circuit implementation
module implementation (
  input  EnableIn,
  input  InputBitIn,
  input  ClkIn,
  output IsEvenOut
);

  wire and_1_out, and_2_out, and_3_out, and_4_out, and_5_out, and_6_out, and_7_out, and_8_out, and_9_out,
       and_10_out, and_11_out, not_1_out, not_2_out, not_3_out, not_4_out, not_5_out, not_6_out, not_7_out,
       not_8_out, not_9_out, not_10_out, not_11_out, not_12_out, not_13_out, not_14_out, not_15_out,
       not_16_out, not_17_out, not_18_out, not_19_out, out0, out1, out2;
  wire [2:0] previousstate;

  Register #(.width(3)) register_1 (
    .D({out2, out1, out0}), .clk(ClkIn), .Q(previousstate), .clr(not_1_out));  // open: en
  not not_1 (not_1_out, EnableIn);
  not not_2 (not_2_out, previousstate[1]);
  and and_1 (and_1_out, not_2_out, previousstate[0], InputBitIn);
  and and_2 (and_2_out, previousstate[1], not_3_out);
  not not_3 (not_3_out, InputBitIn);
  not not_4 (not_4_out, previousstate[2]);
  and and_3 (and_3_out, not_4_out, previousstate[1], previousstate[0]);
  and and_4 (and_4_out, previousstate[2], previousstate[1], not_5_out);
  not not_5 (not_5_out, previousstate[0]);
  not not_6 (not_6_out, previousstate[0]);
  and and_5 (and_5_out, not_6_out, InputBitIn);
  not not_7 (not_7_out, previousstate[2]);
  not not_8 (not_8_out, previousstate[1]);
  and and_6 (and_6_out, not_7_out, not_8_out, previousstate[0]);
  not not_9 (not_9_out, previousstate[2]);
  and and_7 (and_7_out, not_9_out, previousstate[1], not_10_out);
  not not_10 (not_10_out, InputBitIn);
  not not_11 (not_11_out, previousstate[2]);
  not not_12 (not_12_out, previousstate[1]);
  and and_8 (and_8_out, not_11_out, not_12_out, not_13_out);
  not not_13 (not_13_out, InputBitIn);
  not not_14 (not_14_out, previousstate[0]);
  and and_9 (and_9_out, previousstate[1], not_14_out, InputBitIn);
  not not_15 (not_15_out, previousstate[2]);
  and and_10 (and_10_out, not_15_out, previousstate[1], previousstate[0]);
  not not_16 (not_16_out, previousstate[0]);
  and and_11 (and_11_out, previousstate[2], not_16_out, not_17_out);
  not not_17 (not_17_out, InputBitIn);
  not not_18 (not_18_out, previousstate[1]);
  and and_12 (IsEvenOut, previousstate[2], not_18_out, not_19_out);
  not not_19 (not_19_out, previousstate[0]);
  or or_1 (out2, and_1_out, and_2_out, and_3_out, and_4_out);
  or or_2 (out1, and_5_out, and_6_out, and_7_out);
  or or_3 (out0, and_8_out, and_9_out, and_10_out, and_11_out);

  // Other names for the same wires on the sheet: Clk = ClkIn; Enable = EnableIn; InputBit = InputBitIn;
  //   iseven = IsEvenOut
endmodule
