// Logisim project UpDownCounter.circ as structural Verilog: 1 circuit, main circuit implementation
module implementation (
  input  EnableIn,
  input  CountUpIn,
  input  CountDownIn,
  input  clkIn,
  output [2:0] Count
);

  wire and_1_out, and_2_out, and_3_out, and_4_out, and_5_out, and_6_out, and_7_out, and_8_out, and_9_out,
       and_10_out, and_11_out, and_12_out, and_13_out, and_14_out, not_1_out, not_2_out, not_3_out,
       not_4_out, not_5_out, not_6_out, not_7_out, not_8_out, not_9_out, not_10_out, not_11_out, not_12_out,
       not_13_out, or_1_out, or_2_out, or_3_out;

  not not_1 (not_1_out, Count[1]);
  not not_2 (not_2_out, Count[0]);
  not not_3 (not_3_out, CountDownIn);
  not not_4 (not_4_out, CountUpIn);
  not not_5 (not_5_out, Count[1]);
  not not_6 (not_6_out, Count[0]);
  not not_7 (not_7_out, Count[0]);
  not not_8 (not_8_out, CountUpIn);
  not not_9 (not_9_out, CountDownIn);
  not not_10 (not_10_out, Count[0]);
  not not_11 (not_11_out, Count[0]);
  not not_12 (not_12_out, CountDownIn);
  and and_1 (and_1_out, not_1_out, Count[0], CountUpIn);
  and and_2 (and_2_out, Count[1], not_2_out, not_3_out);
  and and_3 (and_3_out, Count[1], Count[0], not_4_out);
  and and_4 (and_4_out, Count[2], not_5_out, not_6_out, CountDownIn);
  and and_5 (and_5_out, Count[2], Count[1], Count[0]);
  and and_6 (and_6_out, not_7_out, CountUpIn);
  and and_7 (and_7_out, Count[0], not_8_out, not_9_out);
  and and_8 (and_8_out, Count[1], not_10_out, CountDownIn);
  and and_9 (and_9_out, Count[2], not_11_out, CountDownIn);
  and and_10 (and_10_out, Count[2], Count[1], CountUpIn);
  and and_11 (and_11_out, Count[1], Count[0], CountUpIn);
  and and_12 (and_12_out, Count[2], not_12_out);
  and and_13 (and_13_out, Count[2], Count[0]);
  and and_14 (and_14_out, Count[2], Count[1]);
  or or_1 (or_1_out, and_1_out, and_2_out, and_3_out, and_4_out, and_5_out);
  or or_2 (or_2_out, and_6_out, and_7_out, and_8_out, and_9_out, and_10_out);
  D_Flip_Flop d_ff_1 (.D(or_3_out), .clk(clkIn), .Q(Count[2]), .reset(not_13_out));  // open: Qn, preset
  or or_3 (or_3_out, and_11_out, and_12_out, and_13_out, and_14_out);
  D_Flip_Flop d_ff_2 (.D(or_1_out), .clk(clkIn), .Q(Count[1]), .reset(not_13_out));  // open: Qn, preset
  D_Flip_Flop d_ff_3 (.D(or_2_out), .clk(clkIn), .Q(Count[0]), .reset(not_13_out));  // open: Qn, preset
  not not_13 (not_13_out, EnableIn);

  // Other names for the same wires on the sheet: clk = clkIn; out0 = Count[0]; out1 = Count[1]; out2 = Count[2];
  //   CountDown = CountDownIn; CountUp = CountUpIn; Enable = EnableIn
endmodule
