// Logisim project Vending.circ as structural Verilog: 1 circuit, main circuit implementation
module implementation (
  input  EnableIn,
  input  QuarterReceivedIn,
  input  DimeReceivedIn,
  input  NickelReceivedIn,
  input  ClkIn,
  output Give_Mechandise_Out,
  output Give_Dime_Out,
  output Give_Nickel_Out
);

  wire and_1_out, and_2_out, and_3_out, and_4_out, and_5_out, and_6_out, and_7_out, and_8_out, and_9_out,
       and_10_out, and_11_out, and_12_out, and_13_out, and_14_out, and_15_out, and_16_out, and_17_out,
       and_18_out, and_19_out, and_20_out, and_21_out, and_22_out, and_23_out, and_24_out, and_25_out,
       and_26_out, and_27_out, and_28_out, and_29_out, and_30_out, and_31_out, and_32_out, not_1_out,
       not_2_out, not_3_out, not_4_out, not_5_out, not_6_out, not_7_out, not_8_out, not_9_out, not_10_out,
       not_11_out, not_12_out, not_13_out, not_14_out, not_15_out, not_16_out, not_17_out, not_18_out,
       not_19_out, not_20_out, not_21_out, not_22_out, not_23_out, not_24_out, not_25_out, not_26_out,
       not_27_out, not_28_out, not_29_out, not_30_out, not_31_out, not_32_out, not_33_out, not_34_out,
       not_35_out, not_36_out, not_37_out, not_38_out, not_39_out, not_40_out, not_41_out, not_42_out,
       not_43_out, not_44_out, not_45_out, not_46_out, not_47_out, not_48_out, not_49_out, not_50_out,
       not_51_out, not_52_out, not_53_out, not_54_out, not_55_out, not_56_out, not_57_out, not_58_out,
       not_59_out, not_60_out, not_61_out, not_62_out, not_63_out, not_64_out, not_65_out, not_66_out, out0,
       out1, out2;
  wire [2:0] previousstate;

  Register #(.width(3)) register_1 (
    .D({out2, out1, out0}), .clk(ClkIn), .Q(previousstate), .clr(not_1_out));  // open: en
  not not_1 (not_1_out, EnableIn);
  not not_2 (not_2_out, previousstate[0]);
  not not_3 (not_3_out, previousstate[2]);
  not not_4 (not_4_out, QuarterReceivedIn);
  and and_1 (and_1_out, not_2_out, not_3_out, not_4_out, DimeReceivedIn, not_5_out);
  not not_5 (not_5_out, NickelReceivedIn);
  not not_6 (not_6_out, previousstate[2]);
  not not_7 (not_7_out, QuarterReceivedIn);
  and and_2 (and_2_out, previousstate[1], not_6_out, not_7_out, not_8_out, NickelReceivedIn);
  not not_8 (not_8_out, DimeReceivedIn);
  not not_9 (not_9_out, QuarterReceivedIn);
  and and_3 (and_3_out, previousstate[0], not_9_out, not_10_out, not_11_out);
  not not_10 (not_10_out, DimeReceivedIn);
  not not_11 (not_11_out, NickelReceivedIn);
  and and_4 (and_4_out, previousstate[0], DimeReceivedIn, NickelReceivedIn);
  and and_5 (and_5_out, previousstate[0], QuarterReceivedIn, NickelReceivedIn);
  and and_6 (and_6_out, previousstate[0], QuarterReceivedIn, NickelReceivedIn);
  not not_12 (not_12_out, previousstate[0]);
  not not_13 (not_13_out, previousstate[1]);
  not not_14 (not_14_out, QuarterReceivedIn);
  and and_7 (and_7_out, not_12_out, not_13_out, not_14_out, not_15_out, NickelReceivedIn);
  not not_15 (not_15_out, DimeReceivedIn);
  not not_16 (not_16_out, previousstate[0]);
  not not_17 (not_17_out, previousstate[2]);
  not not_18 (not_18_out, QuarterReceivedIn);
  and and_8 (and_8_out, not_16_out, not_17_out, not_18_out, not_19_out, NickelReceivedIn);
  not not_19 (not_19_out, DimeReceivedIn);
  not not_20 (not_20_out, previousstate[1]);
  not not_21 (not_21_out, previousstate[2]);
  not not_22 (not_22_out, QuarterReceivedIn);
  and and_9 (and_9_out, not_20_out, not_21_out, not_22_out, DimeReceivedIn, not_23_out);
  not not_23 (not_23_out, NickelReceivedIn);
  not not_24 (not_24_out, previousstate[0]);
  not not_25 (not_25_out, previousstate[1]);
  not not_26 (not_26_out, previousstate[2]);
  and and_10 (and_10_out, not_24_out, not_25_out, not_26_out, QuarterReceivedIn, not_27_out, not_28_out);
  not not_27 (not_27_out, DimeReceivedIn);
  not not_28 (not_28_out, NickelReceivedIn);
  not not_29 (not_29_out, QuarterReceivedIn);
  and and_11 (and_11_out, previousstate[1], not_29_out, not_30_out, not_31_out);
  not not_30 (not_30_out, DimeReceivedIn);
  not not_31 (not_31_out, NickelReceivedIn);
  and and_12 (and_12_out, previousstate[1], DimeReceivedIn, NickelReceivedIn);
  and and_13 (and_13_out, previousstate[1], QuarterReceivedIn, NickelReceivedIn);
  and and_14 (and_14_out, previousstate[1], QuarterReceivedIn, DimeReceivedIn);
  not not_32 (not_32_out, previousstate[0]);
  not not_33 (not_33_out, previousstate[1]);
  not not_34 (not_34_out, previousstate[2]);
  and and_15 (and_15_out, not_32_out, not_33_out, not_34_out, QuarterReceivedIn, not_35_out, not_36_out);
  not not_35 (not_35_out, DimeReceivedIn);
  not not_36 (not_36_out, NickelReceivedIn);
  not not_37 (not_37_out, QuarterReceivedIn);
  and and_16 (and_16_out, previousstate[2], not_37_out, not_38_out, not_39_out);
  not not_38 (not_38_out, DimeReceivedIn);
  not not_39 (not_39_out, NickelReceivedIn);
  not not_40 (not_40_out, previousstate[1]);
  and and_17 (and_17_out, not_40_out, previousstate[2], NickelReceivedIn);
  and and_18 (and_18_out, previousstate[2], DimeReceivedIn, NickelReceivedIn);
  and and_19 (and_19_out, previousstate[2], QuarterReceivedIn, NickelReceivedIn);
  and and_20 (and_20_out, previousstate[2], QuarterReceivedIn, DimeReceivedIn);
  not not_41 (not_41_out, previousstate[1]);
  not not_42 (not_42_out, QuarterReceivedIn);
  and and_21 (and_21_out, previousstate[0], not_41_out, not_42_out, not_43_out, NickelReceivedIn);
  not not_43 (not_43_out, DimeReceivedIn);
  not not_44 (not_44_out, QuarterReceivedIn);
  and and_22 (and_22_out, previousstate[0], not_44_out, DimeReceivedIn, not_45_out);
  not not_45 (not_45_out, NickelReceivedIn);
  or or_1 (out2, and_1_out, and_2_out, and_3_out, and_4_out, and_5_out, and_6_out);
  or or_2 (out1, and_7_out, and_8_out, and_9_out, and_10_out, and_11_out, and_12_out, and_13_out, and_14_out);
  or or_3 (out0, and_15_out, and_16_out, and_17_out, and_18_out, and_19_out, and_20_out, and_21_out, and_22_out);
  not not_46 (not_46_out, QuarterReceivedIn);
  not not_47 (not_47_out, NickelReceivedIn);
  not not_48 (not_48_out, DimeReceivedIn);
  not not_49 (not_49_out, NickelReceivedIn);
  not not_50 (not_50_out, DimeReceivedIn);
  not not_51 (not_51_out, NickelReceivedIn);
  not not_52 (not_52_out, QuarterReceivedIn);
  not not_53 (not_53_out, DimeReceivedIn);
  not not_54 (not_54_out, DimeReceivedIn);
  not not_55 (not_55_out, NickelReceivedIn);
  not not_56 (not_56_out, DimeReceivedIn);
  not not_57 (not_57_out, NickelReceivedIn);
  not not_58 (not_58_out, previousstate[1]);
  not not_59 (not_59_out, DimeReceivedIn);
  not not_60 (not_60_out, NickelReceivedIn);
  not not_61 (not_61_out, DimeReceivedIn);
  not not_62 (not_62_out, NickelReceivedIn);
  not not_63 (not_63_out, QuarterReceivedIn);
  not not_64 (not_64_out, NickelReceivedIn);
  not not_65 (not_65_out, DimeReceivedIn);
  not not_66 (not_66_out, NickelReceivedIn);
  and and_23 (and_23_out, previousstate[2], not_46_out, DimeReceivedIn, not_47_out);
  and and_24 (and_24_out, previousstate[2], QuarterReceivedIn, not_48_out, not_49_out);
  and and_25 (and_25_out, previousstate[1], QuarterReceivedIn, not_50_out, not_51_out);
  and and_26 (and_26_out, previousstate[1], previousstate[2], not_52_out, not_53_out, NickelReceivedIn);
  and and_27 (and_27_out, previousstate[0], QuarterReceivedIn, not_54_out, not_55_out);
  and and_28 (and_28_out, previousstate[2], QuarterReceivedIn, not_56_out, not_57_out);
  and and_29 (and_29_out, previousstate[0], not_58_out, QuarterReceivedIn, not_59_out, not_60_out);
  and and_30 (and_30_out, previousstate[2], QuarterReceivedIn, not_61_out, not_62_out);
  and and_31 (and_31_out, previousstate[1], previousstate[2], not_63_out, DimeReceivedIn, not_64_out);
  and and_32 (and_32_out, previousstate[0], previousstate[1], QuarterReceivedIn, not_65_out, not_66_out);
  or or_4 (Give_Mechandise_Out, and_23_out, and_24_out, and_25_out, and_26_out, and_27_out);
  or or_5 (Give_Dime_Out, and_28_out, and_29_out);
  or or_6 (Give_Nickel_Out, and_30_out, and_31_out, and_32_out);

  // Other names for the same wires on the sheet: clk = ClkIn; dimeout = Give_Dime_Out; DimeReceieved = DimeReceivedIn;
  //   Enable = EnableIn; merchout = Give_Mechandise_Out; nickelout = Give_Nickel_Out;
  //   NickelReceieved = NickelReceivedIn; QuarterReceieved = QuarterReceivedIn
endmodule
