// Logisim project CPUgrader.circ as structural Verilog: 1 circuit, main circuit main
module main (
  output [4:0] Instruction_Address_Out,
  output [3:0] Reg0_Out,
  output [3:0] Reg1_Out,
  output [3:0] Reg2_Out,
  output [3:0] Reg3_Out,
  output [3:0] Reg4_Out,
  output [3:0] Reg5_Out,
  output [3:0] Reg6_Out,
  output [3:0] Reg7_Out,
  output [3:0] Reg8_Out,
  output [3:0] Reg9_Out,
  output [3:0] Reg10_Out,
  output [3:0] Reg11_Out,
  output [3:0] Reg12_Out,
  output [3:0] Reg13_Out,
  output [3:0] Reg14_Out,
  output [3:0] Reg15_Out,
  output clk_out,
  output halt
);

  wire [15:0] Instruction;

  Clock clock_1 (.out(clk_out));
  ROM #(.addrWidth(5), .dataWidth(16)) Instruction_Memory (.addr(Instruction_Address_Out), .data(Instruction));
  // Probe on Instruction
  // Probe on Reg0_Out
  // Probe on Reg4_Out
  // Probe on Reg8_Out
  // Probe on Reg12_Out
  // Probe on Reg1_Out
  // Probe on Reg5_Out
  // Probe on Reg9_Out
  // Probe on Reg13_Out
  // Probe on Reg2_Out
  // Probe on Reg6_Out
  // Probe on Reg10_Out
  // Probe on Reg14_Out
  implementation implementation_1 (
    .Instruction_In(Instruction), .ClkIn(clk_out), .Instruction_Address_Out(Instruction_Address_Out),
    .Reg0_Out(Reg0_Out), .Reg1_Out(Reg1_Out), .Reg2_Out(Reg2_Out), .Reg3_Out(Reg3_Out), .Reg4_Out(Reg4_Out),
    .Reg5_Out(Reg5_Out), .Reg6_Out(Reg6_Out), .Reg7_Out(Reg7_Out), .Reg8_Out(Reg8_Out), .Reg9_Out(Reg9_Out),
    .Reg10_Out(Reg10_Out), .Reg11_Out(Reg11_Out), .Reg12_Out(Reg12_Out), .Reg13_Out(Reg13_Out),
    .Reg14_Out(Reg14_Out), .Reg15_Out(Reg15_Out));
  // Probe on Reg3_Out
  // Probe on Reg7_Out
  // Probe on Reg11_Out
  // Probe on Reg15_Out
  Counter #(.max('h16), .ongoal("stay"), .width(6)) counter_1 (
    .count(1'b1), .clk(clk_out), .carry(halt));  // open: clr, load, up, D, Q
  // Probe on Instruction_Address_Out

  // Other names for the same wires on the sheet: Clk = clk_out; Instruction_Address[4:0] = Instruction_Address_Out;
  //   Reg0[3:0] = Reg0_Out; Reg1[3:0] = Reg1_Out; Reg2[3:0] = Reg2_Out; Reg3[3:0] = Reg3_Out; Reg4[3:0] = Reg4_Out;
  //   Reg5[3:0] = Reg5_Out; Reg6[3:0] = Reg6_Out; Reg7[3:0] = Reg7_Out; Reg8[3:0] = Reg8_Out; Reg9[3:0] = Reg9_Out;
  //   Reg10[3:0] = Reg10_Out; Reg11[3:0] = Reg11_Out; Reg12[3:0] = Reg12_Out; Reg13[3:0] = Reg13_Out;
  //   Reg14[3:0] = Reg14_Out; Reg15[3:0] = Reg15_Out; Stop_Testing = halt

  // Notes on the sheet:
  //   contents of Instruction_Memory (hex, n*v repeats v):
  //   2003 2106 1005 3210 4301 5433 6520 763c 8720 986f b938 ca77 db13 ec62 fd85 af82 41cd b552 1075 ce52
  //   877e 7223 fddc e05 2f8d
endmodule
